# Fritzing sketch pico-LoRa (saved by Fritzing 0.9.10b)
breadboards: 1

parts:
  A1 = Waveshare rp2040-zero tht [package=THT]
  LoRa_Module1 = Ra-01 - LoRa Module SX1278 [part_number=SX1278]

nets:
  N1: A1.Pin_2, LoRa_Module1.GND
  N2: A1.Pin_3, LoRa_Module1.3.3V
  N3: A1.Pin_15, LoRa_Module1.NSS
  N4: A1.Pin_16, LoRa_Module1.DIO0
  N5: A1.Pin_17, LoRa_Module1.RESET
  N6: A1.Pin_19, LoRa_Module1.MISO
  N7: A1.Pin_20, LoRa_Module1.MOSI
  N8: A1.Pin_21, LoRa_Module1.SCK

custom parts:
  Waveshare rp2040-zero tht: .RP2040-Zero, A Low-Cost, High-Performance Pico-Like MCU Board Based On Raspberry Pi Microcontroller RP2040. This varant is THT without the extra connections.
  Ra-01 - LoRa Module SX1278: The Ra-01 LoRa Module featuring the SX1278 engine by Semtech. Module by AI-Thinker. Module (Ra-01) specifications from: https://www.banggood.com/Ra-01-Smart-Electronics-SX1278-LoRa-Spread-Spectrum-Wireless-Module-Ultra-Far-10KM-433M-p-1130769.html Description: Power supply: DC1.8-3.7V(3.3V) Chip: SX1278 Frequency: 433Mhz Operating temperature: -40~+85°C On Sheild Description (may vary by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
